// Logisim project SymulatorProfesora.circ as structural Verilog: 1 circuit, main circuit main
module main (
  input  in_1,
  input  in_2,
  input  send
);

  wire clock_1_out, clock_2_out, comparator_1_eq, comparator_2_eq, key_reset_out, keyboard_1_avail,
       main_1_output, main_4_done, or_1_out, pull_resistor_1_node;
  wire [4:0] adder_1_out, counter_1_q, counter_2_q, register_2_q;
  wire [6:0] keyboard_1_data, main_2_output, register_1_q;
  wire [31:0] main_3_output, main_4_out_4, main_4_out_5, main_4_out_6, main_4_out_7, main_4_out_8,
       main_4_out_9, main_4_out_10, main_4_out_11, main_4_out_12, main_4_out_13, main_4_out_14,
       main_4_out_15, main_4_out_16, main_4_out_17, main_4_out_18, main_4_out_19, main_4_out_20,
       main_4_out_21, main_4_out_22, main_4_out_23, main_4_out_24, main_4_out_25, main_4_out_26,
       main_4_out_27, main_4_out_28, main_4_out_29, main_4_out_30, main_4_out_31, main_4_out_32,
       main_4_out_33, main_4_out_34, main_4_out_35, or_2_out, rom_1_data, rom_2_data;

  Pull_Resistor pull_resistor_1 (.node(pull_resistor_1_node));
  assign pull_resistor_1_node = keyboard_1_avail ? clock_1_out : 1'bz;  // Controlled_Buffer controlled_buffer_1
  Keyboard keyboard_1 (
    .clk(pull_resistor_1_node), .re(1'b1), .avail(keyboard_1_avail), .data(keyboard_1_data));  // open: clr
  Register #(.width(7)) register_1 (
    .D(keyboard_1_data), .Q(register_1_q), .clk(pull_resistor_1_node), .clr(key_reset_out));  // open: en
  not key_reset (key_reset_out, clock_1_out);
  Comparator #(.width(7), .mode("unsigned")) comparator_1 (
    .a(register_1_q), .b(7'b1100100), .eq(comparator_1_eq));  // open: gt, lt
  Comparator #(.width(7), .mode("unsigned")) comparator_2 (
    .a(register_1_q), .b(7'b1100001), .eq(comparator_2_eq));  // open: gt, lt
  Counter #(.width(5), .max('h1b), .ongoal("stay")) counter_1 (
    .load(comparator_1_eq), .Q(counter_1_q), .clk(or_1_out));  // open: D, count, carry, clr
  or or_1 (or_1_out, comparator_1_eq, comparator_2_eq);
  Counter #(.width(5), .max('h1f)) counter_2 (.Q(counter_2_q), .clk(clock_1_out));  // open: load, D, count, carry, clr
  Clock clock_1 (.out(clock_1_out));
  Clock clock_2 (.out(clock_2_out));
  Register #(.width(5)) register_2 (.D(counter_1_q), .Q(register_2_q), .clk(main_4_done));  // open: en, clr
  Adder #(.width(5)) adder_1 (.a(register_2_q), .b(counter_2_q), .out(adder_1_out));  // open: cin, cout
  single_pulse_generator_main main_1 (.trigger(in_1), .\output (main_1_output), .clock(clock_2_out));
  ROM #(.addrWidth(5), .dataWidth(32)) rom_1 (.addr(counter_2_q), .data(rom_1_data));  // open: sel
  ROM #(.addrWidth(5), .dataWidth(32)) rom_2 (.addr(adder_1_out), .data(rom_2_data));  // open: sel
  ROM_message_spitter_main main_2 (
    .clock(clock_2_out), .\output (main_2_output), .trigger(main_1_output), .reset(in_2));
  TTY #(.rows(1), .cols(110)) tty_1 (.data(main_2_output), .clk(clock_2_out), .clr(main_1_output));  // open: we
  student_drop_main main_3 (.\input (rom_1_data), .send(send), .\output (main_3_output));
  display_buffer_main main_4 (
    .Address(or_2_out), .Select(counter_2_q), .out_4(main_4_out_4), .out_5(main_4_out_5),
    .out_6(main_4_out_6), .out_7(main_4_out_7), .out_8(main_4_out_8), .out_9(main_4_out_9),
    .out_10(main_4_out_10), .out_11(main_4_out_11), .out_12(main_4_out_12), .out_13(main_4_out_13),
    .out_14(main_4_out_14), .out_15(main_4_out_15), .out_16(main_4_out_16), .out_17(main_4_out_17),
    .out_18(main_4_out_18), .out_19(main_4_out_19), .out_20(main_4_out_20), .out_21(main_4_out_21),
    .out_22(main_4_out_22), .out_23(main_4_out_23), .out_24(main_4_out_24), .out_25(main_4_out_25),
    .out_26(main_4_out_26), .out_27(main_4_out_27), .out_28(main_4_out_28), .out_29(main_4_out_29),
    .out_30(main_4_out_30), .out_31(main_4_out_31), .out_32(main_4_out_32), .out_33(main_4_out_33),
    .out_34(main_4_out_34), .out_35(main_4_out_35), .Done(main_4_done));
  assign or_2_out = main_3_output | rom_2_data;  // OR_Gate or_2, 32 bits wide
  DotMatrix #(.matrixcols(32), .matrixrows(32)) dotmatrix_1 (
    .col0(main_4_out_4), .col1(main_4_out_5), .col2(main_4_out_6), .col3(main_4_out_7), .col4(main_4_out_8),
    .col5(main_4_out_9), .col6(main_4_out_10), .col7(main_4_out_11), .col8(main_4_out_12),
    .col9(main_4_out_13), .col10(main_4_out_14), .col11(main_4_out_15), .col12(main_4_out_16),
    .col13(main_4_out_17), .col14(main_4_out_18), .col15(main_4_out_19), .col16(main_4_out_20),
    .col17(main_4_out_21), .col18(main_4_out_22), .col19(main_4_out_23), .col20(main_4_out_24),
    .col21(main_4_out_25), .col22(main_4_out_26), .col23(main_4_out_27), .col24(main_4_out_28),
    .col25(main_4_out_29), .col26(main_4_out_30), .col27(main_4_out_31), .col28(main_4_out_32),
    .col29(main_4_out_33), .col30(main_4_out_34), .col31(main_4_out_35));

  // Notes on the sheet:
  //   keyboard
  //   d
  //   a
  //   Zegar:szybko
  //   student
  //   profesor
  //   contents of rom_1 (hex, n*v repeats v):
  //   28*0 50000000 e0000000 50000000
  //   contents of rom_2 (hex, n*v repeats v):
  //   27*0 4 7 e 7 4
endmodule
